# Fritzing sketch circuit (saved by Fritzing 0.9.4)

parts:
  Part1 = Arduino Uno (Rev3) - ICSP
  M1 = LJ18A3-H-ZBX [package=THT]
  Part2 = LCD1602-I2C
  S1 = Round Pushbutton
  S2 = Round Pushbutton
  A1 = MH-FMD buzzer
  S3 = Round Pushbutton
  R1 = Resistor [tolerance=±5% resistance=10k package="2010 [SMD]"]
  R2 = Resistor [tolerance=±5% resistance=10k package="2010 [SMD]"]
  R3 = Resistor [tolerance=±5% resistance=10k package="2010 [SMD]"]

nets:
  5V: Part1.5V, M1.VI_(BRN), Part2.VCC, A1.Pin_1
  N1: Part1.D8, S3.leg1, R3.Pin_0
  N2: Part1.D10_PWM/SS, S1.leg1, R1.Pin_0
  GND: Part1.GND, M1.VO_(BLU), Part2.GND, S2.leg0, A1.Pin_3, S3.leg0
  N3: Part1.A4/SDA, Part2.SDA
  N4: Part1.A5/SCL, Part2.SCL
  N5: Part1.D2, M1.SIG_(BLK)
  N6: Part1.D3_PWM, A1.Pin_2
  N7: S2.leg1, R2.Pin_0
  N8: R1.Pin_1, R3.Pin_1

custom parts:
  LJ18A3-H-ZBX: LJ18A3-H-ZBX Proximity Sensor module.
  LCD1602-I2C: A standard character display, usually with 2x16 characters. Comes in many colors with LCM1602 IIC attached.
  MH-FMD buzzer: MH-FMD buzzer.
